# Fritzing sketch WebPixelFrame (saved by Fritzing 0.9.3b)
circuit board: 4.12827cm x 7.00423cm
breadboards: 1

parts:
  WeMos_D1_Mini2 = WeMos D1 Mini
  U11 = mystery part, 1 pin [chip_label=?]
  U12 = mystery part, 1 pin [chip_label=?]
  U18 = mystery part, 1 pin [chip_label=?]
  U19 = mystery part, 6 pins [chip_label=?]
  U21 = mystery part, 6 pins [chip_label=?]
  U22 = mystery part, 1 pin [chip_label=?]
  U23 = mystery part, 1 pin [chip_label=Data]
  U24 = mystery part, 1 pin [chip_label=?]
  U25 = mystery part, 1 pin [chip_label=?]
  U26 = mystery part, 1 pin [chip_label=?]  # not connected

nets:
  N1: WeMos_D1_Mini2.3V3, U11.pin1
  N2: WeMos_D1_Mini2.5V, U18.pin1, U21.pin6, U25.pin1
  N3: WeMos_D1_Mini2.G, U19.pin5, U21.pin5, U22.pin1, U24.pin1
  N4: WeMos_D1_Mini2.RX, U19.pin1
  N5: U12.pin1, U19.pin6
  N6: U21.pin1, U23.pin1

notes:
  5v
